# Fritzing sketch BrightnessControlWithPot (saved by Fritzing 0.9.9b)
breadboards: 1

parts:
  Mod1 = Raspberry Pi 4B
  INA1 = INA219 DC Current Sensor Breakout
  7SEG1 = 7-Segment LED I2C Backpack (blue)
  R1 = Resistor [tolerance=±5% power=0.25 resistance=3.3k package=THT]
  R3 = Resistor [tolerance=±5% power=0.25 resistance=3.3k package=THT]
  Led = LED - 5mm [color="Red (633nm)" current=0.030 package="5 mm [THT]"]
  R5 = Rotary Potentiometer (Small) [maximum_resistance=100kΩ package=THT]

nets:
  5V: Mod1.5V, INA1.VCC, 7SEG1.V+, R1.Pin_1
  N1: Mod1.GPIO2, INA1.SDA, 7SEG1.SDA
  N2: Mod1.GPIO3, INA1.SCL, 7SEG1.SCL
  GND: Mod1.GND, INA1.GND, 7SEG1.GND, Led.cathode, R5.wiper, R5.leg2
  N3: Mod1.GPIO18, R3.Pin_0
  N4: INA1.Vin-, R5.leg1
  N5: INA1.Vin+, R1.Pin_0
  N6: R3.Pin_1, Led.anode

custom parts:
  INA219 DC Current Sensor Breakout: INA DC Current Sensor Breakout
  7-Segment LED I2C Backpack (blue): 4-digit, 7-segment LED Display with I2C Control
